// Logisim project e2237386simple.circ as structural Verilog: 1 circuit, main circuit main
module main (
  input  A,
  input  B,
  input  C,
  input  D,
  output O
);

  wire and_1_out, and_2_out, and_3_out, not_1_out, not_2_out;

  not not_1 (not_1_out, B);
  not not_2 (not_2_out, D);
  and and_1 (and_1_out, A, C);
  and and_2 (and_2_out, not_2_out, not_1_out);
  and and_3 (and_3_out, A, and_2_out);
  or or_1 (O, and_1_out, and_3_out);
endmodule
