// Logisim project e2237386Demux.circ as structural Verilog: 1 circuit, main circuit main
module main (
  input  I0,
  input  I1,
  input  S1,
  input  S0,
  output out_5,
  output out_6,
  output out_7,
  output out_8
);

  // _2_to_4_Decoder__x2___74155 #(.Facing("east")) 2_to_4_decoder_x2_74155_1: pin names not known; wires that end beside it: 1'b1, I0, I1, S0, S0, 1'b0, S1, S1, out_5, out_6, out_7, out_8, 1'b0, 1'b0
endmodule
