// Logisim project e2237386Encoder.circ as structural Verilog: 1 circuit, main circuit main
module main (
  input  I0,
  input  I1,
  input  I2,
  input  I3,
  input  I4,
  input  I5,
  input  I6,
  input  I7,
  output O2,
  output O1,
  output O0
);

  wire or_1_out, or_2_out, or_3_out, or_5_out, or_6_out;

  or or_1 (or_1_out, I2, I0);
  or or_2 (or_2_out, I4, I6);
  or or_3 (or_3_out, I4, I5);
  or or_4 (O0, or_2_out, or_1_out);
  or or_5 (or_5_out, I0, I1);
  or or_6 (or_6_out, I2, I3);
  or or_7 (O2, or_5_out, or_6_out);
  or or_8 (O1, or_5_out, or_3_out);
endmodule
