// Logisim project e2237386Mux.circ as structural Verilog: 1 circuit, main circuit main
module main (
  input  I0,
  input  I1,
  input  I2,
  input  I3,
  input  S2,
  input  S3,
  input  S0,
  input  S1,
  input  I4,
  input  I5,
  input  I6,
  input  I7,
  input  I8,
  input  I9,
  input  I10,
  output O
);

  wire n4_to_1_mux_x2_74153_1_p13, n4_to_1_mux_x2_74153_1_p14, n4_to_1_mux_x2_74153_2_p8;

  // _4_to_1_MUX__x2___74153 #(.Facing("east")) 4_to_1_mux_x2_74153_1: pin names not known; wires that end beside it: I0, I1, I2, I3, I4, I5, I6, I7, 1'b0, S0, 1'b0, S1, n4_to_1_mux_x2_74153_1_p13, n4_to_1_mux_x2_74153_1_p14
  // _4_to_1_MUX__x2___74153 #(.Facing("east")) 4_to_1_mux_x2_74153_2: pin names not known; wires that end beside it: I8, I9, I10, 1'b0, S0, 1'b0, S1, n4_to_1_mux_x2_74153_2_p8
  // _4_to_1_MUX__x2___74153 #(.Facing("east")) 4_to_1_mux_x2_74153_3: pin names not known; wires that end beside it: n4_to_1_mux_x2_74153_1_p13, n4_to_1_mux_x2_74153_1_p14, n4_to_1_mux_x2_74153_2_p8, 1'b0, S2, 1'b0, S3, O
endmodule
