// Logisim project e2237386.circ as structural Verilog: 1 circuit, main circuit main
module main (
  input  A1,
  input  A0,
  input  B1,
  input  B0,
  input  O1,
  input  O0,
  input  S,
  output N,
  output B,
  output G,
  output E,
  output L,
  output L0,
  output L1,
  output L2,
  output L3,
  output L4,
  output L5,
  output L6,
  output L7
);

  wire and_1_out, and_2_out, and_3_out, and_4_out, and_5_out, and_6_out, and_7_out, and_8_out, and_9_out,
       and_10_out, and_11_out, and_12_out, and_13_out, and_14_out, and_15_out, and_16_out, and_17_out,
       and_18_out, and_19_out, and_20_out, and_21_out, and_22_out, and_23_out, and_24_out, and_25_out,
       and_26_out, and_27_out, and_28_out, and_29_out, and_30_out, and_31_out, and_32_out, and_33_out,
       and_34_out, and_35_out, and_36_out, and_37_out, and_38_out, and_39_out, and_40_out, and_41_out,
       and_42_out, and_43_out, and_44_out, and_45_out, and_46_out, and_47_out, and_48_out, and_49_out,
       and_50_out, and_51_out, and_52_out, and_53_out, and_54_out, and_55_out, n3_to_8_decoder_74138_1_p7,
       n3_to_8_decoder_74138_1_p8, n3_to_8_decoder_74138_1_p9, n3_to_8_decoder_74138_1_p10,
       n3_to_8_decoder_74138_1_p11, n3_to_8_decoder_74138_1_p12, n3_to_8_decoder_74138_1_p13,
       n3_to_8_decoder_74138_1_p14, n4_to_1_mux_x2_74153_1_p13, n4_to_1_mux_x2_74153_1_p14,
       n4_to_1_mux_x2_74153_2_p9, not_1_out, not_2_out, not_3_out, not_4_out, not_5_out, not_6_out,
       not_7_out, or_1_out, or_2_out, or_3_out, or_4_out, or_5_out, or_6_out, or_7_out, or_8_out, or_9_out,
       or_10_out, or_11_out, or_12_out, or_13_out, or_14_out, or_15_out, or_16_out, or_17_out, or_18_out,
       or_19_out, or_20_out;

  not not_1 (not_1_out, A1);
  not not_2 (not_2_out, A0);
  not not_3 (not_3_out, B1);
  not not_4 (not_4_out, B0);
  not not_5 (not_5_out, O1);
  not not_6 (not_6_out, O0);
  not not_7 (not_7_out, S);
  and and_1 (and_1_out, not_1_out, B1);
  and and_2 (and_2_out, not_1_out, not_2_out);
  and and_3 (and_3_out, not_2_out, B1);
  and and_4 (and_4_out, not_2_out, not_4_out);
  and and_5 (and_5_out, A0, B0);
  and and_6 (and_6_out, not_1_out, not_3_out);
  and and_7 (and_7_out, A1, B1);
  and and_8 (and_8_out, A1, not_3_out);
  and and_9 (and_9_out, A1, A0);
  and and_10 (and_10_out, A0, not_3_out);
  and and_11 (and_11_out, A0, not_4_out);
  and and_12 (and_12_out, A1, B0);
  and and_13 (and_13_out, not_1_out, B1);
  and and_14 (and_14_out, not_1_out, not_2_out);
  and and_15 (and_15_out, not_2_out, B1);
  and and_16 (and_16_out, A1, B1);
  and and_17 (and_17_out, A0, B1);
  and and_18 (and_18_out, A1, A0);
  and and_19 (and_19_out, and_2_out, B0);
  and and_20 (and_20_out, and_3_out, B0);
  or or_1 (or_1_out, and_4_out, and_5_out);
  or or_2 (or_2_out, and_6_out, and_7_out);
  and and_21 (and_21_out, and_9_out, not_4_out);
  and and_22 (and_22_out, and_10_out, not_4_out);
  or or_3 (or_3_out, and_11_out, and_12_out);
  and and_23 (and_23_out, and_14_out, B0);
  and and_24 (and_24_out, and_15_out, B0);
  and and_25 (and_25_out, and_17_out, B0);
  and and_26 (and_26_out, and_18_out, B0);
  and and_27 (and_27_out, O0, O1);
  and and_28 (and_28_out, O0, not_5_out);
  and and_29 (and_29_out, not_5_out, not_6_out);
  or or_4 (or_4_out, and_1_out, and_19_out);
  and and_30 (and_30_out, or_1_out, or_2_out);
  or or_5 (or_5_out, and_8_out, and_21_out);
  or or_6 (or_6_out, and_13_out, and_23_out);
  or or_7 (or_7_out, and_16_out, and_25_out);
  and and_31 (and_31_out, not_1_out, not_2_out);
  and and_32 (and_32_out, and_31_out, B1);
  and and_33 (and_33_out, not_1_out, B1);
  and and_34 (and_34_out, and_33_out, not_4_out);
  and and_35 (and_35_out, A1, not_2_out);
  and and_36 (and_36_out, and_35_out, not_3_out);
  and and_37 (and_37_out, A1, not_3_out);
  and and_38 (and_38_out, and_37_out, not_4_out);
  and and_39 (and_39_out, not_1_out, A0);
  and and_40 (and_40_out, and_39_out, and_41_out);
  and and_41 (and_41_out, not_3_out, B0);
  and and_42 (and_42_out, A1, A0);
  and and_43 (and_43_out, and_42_out, and_44_out);
  and and_44 (and_44_out, B1, B0);
  and and_45 (and_45_out, not_1_out, not_2_out);
  and and_46 (and_46_out, and_45_out, B1);
  and and_47 (and_47_out, not_1_out, B1);
  and and_48 (and_48_out, and_47_out, B0);
  and and_49 (and_49_out, A1, not_3_out);
  and and_50 (and_50_out, and_49_out, not_4_out);
  and and_51 (and_51_out, A1, A0);
  and and_52 (and_52_out, and_51_out, not_3_out);
  and and_53 (and_53_out, not_2_out, B0);
  or or_8 (or_8_out, and_53_out, and_54_out);
  and and_54 (and_54_out, A0, not_4_out);
  and and_55 (and_55_out, and_27_out, S);
  or or_9 (or_9_out, or_4_out, and_20_out);
  or or_10 (or_10_out, or_5_out, and_22_out);
  or or_11 (or_11_out, or_6_out, and_24_out);
  or or_12 (or_12_out, or_7_out, and_26_out);
  or or_13 (or_13_out, and_32_out, and_34_out);
  or or_14 (or_14_out, and_36_out, and_38_out);
  or or_15 (or_15_out, and_40_out, and_43_out);
  or or_16 (or_16_out, and_46_out, and_48_out);
  or or_17 (or_17_out, and_50_out, and_52_out);
  or or_18 (or_18_out, or_13_out, or_14_out);
  or or_19 (or_19_out, or_18_out, or_15_out);
  or or_20 (or_20_out, or_16_out, or_17_out);
  and and_56 (N, and_55_out, or_11_out);
  and and_57 (B, and_28_out, or_3_out);
  and and_58 (G, and_29_out, or_10_out);
  and and_59 (E, and_29_out, and_30_out);
  and and_60 (L, and_29_out, or_9_out);
  // _4_to_1_MUX__x2___74153 #(.Facing("east")) 4_to_1_mux_x2_74153_1: pin names not known; wires that end beside it: 1'b0, A1, or_12_out, 1'b0, 1'b0, A0, or_19_out, or_20_out, 1'b0, S, 1'b0, O0, n4_to_1_mux_x2_74153_1_p13, n4_to_1_mux_x2_74153_1_p14
  // _4_to_1_MUX__x2___74153 #(.Facing("east")) 4_to_1_mux_x2_74153_2: pin names not known; wires that end beside it: A1, 1'b0, or_8_out, or_8_out, 1'b0, S, 1'b0, O0, n4_to_1_mux_x2_74153_2_p9
  // _3_to_8_decoder__74138 #(.Facing("east")) 3_to_8_decoder_74138_1: pin names not known; wires that end beside it: n4_to_1_mux_x2_74153_2_p9, n4_to_1_mux_x2_74153_1_p14, n4_to_1_mux_x2_74153_1_p13, O1, 1'b0, 1'b0, n3_to_8_decoder_74138_1_p7, n3_to_8_decoder_74138_1_p8, n3_to_8_decoder_74138_1_p9, n3_to_8_decoder_74138_1_p10, n3_to_8_decoder_74138_1_p11, n3_to_8_decoder_74138_1_p12, n3_to_8_decoder_74138_1_p13, n3_to_8_decoder_74138_1_p14
  not not_8 (L0, n3_to_8_decoder_74138_1_p7);
  not not_9 (L1, n3_to_8_decoder_74138_1_p8);
  not not_10 (L2, n3_to_8_decoder_74138_1_p9);
  not not_11 (L3, n3_to_8_decoder_74138_1_p10);
  not not_12 (L4, n3_to_8_decoder_74138_1_p11);
  not not_13 (L5, n3_to_8_decoder_74138_1_p12);
  not not_14 (L6, n3_to_8_decoder_74138_1_p13);
  not not_15 (L7, n3_to_8_decoder_74138_1_p14);
endmodule
